# Fritzing sketch simon_button (saved by Fritzing 0.9.3b)

parts:
  WeMos_D1_Mini1 = WeMos D1 Mini
  S1 = Round Pushbutton
  S2 = Round Pushbutton
  S3 = Round Pushbutton
  S4 = Round Pushbutton
  LED1 = smd LED [color="Red (633nm)" package="0805 [SMD]"]
  LED2 = smd LED [color="Yellow (595nm)" package="0805 [SMD]"]
  LED3 = smd LED [color="Blue (505nm)" package="0805 [SMD]"]
  LED4 = smd LED [color="Green (565nm)" package="0805 [SMD]"]

nets:
  N1: WeMos_D1_Mini1.D0, LED1.anode
  N2: WeMos_D1_Mini1.D1, LED2.anode
  N3: WeMos_D1_Mini1.D2, LED3.anode
  N4: WeMos_D1_Mini1.D3, LED4.anode
  N5: WeMos_D1_Mini1.D4, S1.leg0
  N6: WeMos_D1_Mini1.D5, S2.leg0
  N7: WeMos_D1_Mini1.D6, S3.leg0
  N8: WeMos_D1_Mini1.D7, S4.leg0
  N9: WeMos_D1_Mini1.G, S1.leg1, S2.leg1, S3.leg1, S4.leg1, LED1.cathode, LED2.cathode, LED3.cathode, LED4.cathode
